// Logisim project BasicComputer.circ as structural Verilog: 9 circuits, main circuit main
module main (
  input  [3:0] INP,
  input  A,
  input  B,
  input  Sub_or_Add,
  input  [2:0] CODE,
  input  CS,
  input  READ,
  input  OE,
  input  [2:0] OPselect,
  input  [1:0] select_shift,
  output [3:0] A_2,
  output carry,
  output [3:0] B_2,
  output [3:0] OUTP
);

  wire clock_1_out;
  wire [2:0] comprator_1_a_b;
  wire [3:0] add_sub_1_result, complement_1_b, dec_1_out_2, inc_1_out_2, memory_1_out_6, multiplexer_1_out,
       shift_1_b;

  Clock clock_1 (.out(clock_1_out));
  MEMORY memory_1 (.in_1(INP), .in_2(CODE), .CS(CS), .RD(READ), .OE(OE), .out_6(memory_1_out_6));
  Register #(.width(4)) register_1 (.D(memory_1_out_6), .en(B), .Q(B_2), .clk(clock_1_out));  // open: clr
  Register #(.width(4)) register_2 (.D(memory_1_out_6), .en(A), .Q(A_2), .clk(clock_1_out));  // open: clr
  ADD_SUB add_sub_1 (.k(Sub_or_Add), .A(A_2), .B(B_2), .result(add_sub_1_result), .c(carry));
  COMPRATOR comprator_1 (
    .A(A_2), .B(B_2), .A_B(comprator_1_a_b[0]), .A_B_2(comprator_1_a_b[1]), .A___B(comprator_1_a_b[2]));
  SHIFT shift_1 (.A(A_2), .in_2(select_shift), .clock(clock_1_out), .B(shift_1_b));
  INC inc_1 (.A(A_2), .out_2(inc_1_out_2));
  DEC dec_1 (.A(A_2), .out_2(dec_1_out_2));
  COMPLEMENT complement_1 (.A(A_2), .B(complement_1_b));
  Multiplexer #(.select(3), .width(4)) multiplexer_1 (
    .in0(add_sub_1_result), .in1({1'b0, comprator_1_a_b}), .in2(shift_1_b), .in3(inc_1_out_2),
    .in4(dec_1_out_2), .in5(complement_1_b), .out(multiplexer_1_out), .sel(OPselect));  // open: in6, in7, en
  Register #(.width(4)) register_3 (.D(multiplexer_1_out), .en(1'b1), .Q(OUTP), .clk(clock_1_out));  // open: clr
endmodule

// RAM
module MEMORY (
  input  [3:0] in_1,
  input  [2:0] in_2,
  input  CS,
  input  RD,
  input  OE,
  output [3:0] out_6
);

  wire and_1_out, and_2_out, and_3_out, and_4_out, and_5_out, and_6_out, and_7_out, and_8_out, and_9_out,
       and_10_out, and_11_out, and_12_out, and_13_out, and_14_out, and_15_out, and_16_out, and_17_out,
       and_18_out, and_19_out, and_20_out, and_21_out, and_22_out, and_23_out, and_24_out, and_25_out,
       and_26_out, and_27_out, and_28_out, and_29_out, and_30_out, and_31_out, and_32_out, and_33_out,
       and_34_out, and_35_out, and_36_out, and_37_out, and_38_out, and_39_out, and_40_out, and_41_out,
       and_42_out, d_ff_1_q, d_ff_2_q, d_ff_3_q, d_ff_4_q, d_ff_5_q, d_ff_6_q, d_ff_7_q, d_ff_8_q, d_ff_9_q,
       d_ff_10_q, d_ff_11_q, d_ff_12_q, d_ff_13_q, d_ff_14_q, d_ff_15_q, d_ff_16_q, d_ff_17_q, d_ff_18_q,
       d_ff_19_q, d_ff_20_q, d_ff_21_q, d_ff_22_q, d_ff_23_q, d_ff_24_q, d_ff_25_q, d_ff_26_q, d_ff_27_q,
       d_ff_28_q, d_ff_29_q, d_ff_30_q, d_ff_31_q, d_ff_32_q, decoder_1_out0, decoder_1_out1, decoder_1_out2,
       decoder_1_out3, decoder_1_out4, decoder_1_out5, decoder_1_out6, decoder_1_out7, not_1_out, or_1_out,
       or_2_out, or_3_out, or_4_out;

  Decoder #(.select(3)) decoder_1 (
    .out0(decoder_1_out0), .out1(decoder_1_out1), .out2(decoder_1_out2), .out3(decoder_1_out3),
    .out4(decoder_1_out4), .out5(decoder_1_out5), .out6(decoder_1_out6), .out7(decoder_1_out7), .sel(in_2));  // open: en
  and and_1 (and_1_out, CS, not_1_out);
  not not_1 (not_1_out, RD);
  and and_2 (and_2_out, and_1_out, decoder_1_out0);
  and and_3 (and_3_out, and_1_out, decoder_1_out1);
  and and_4 (and_4_out, and_1_out, decoder_1_out2);
  and and_5 (and_5_out, and_1_out, decoder_1_out3);
  and and_6 (and_6_out, and_1_out, decoder_1_out4);
  and and_7 (and_7_out, and_1_out, decoder_1_out5);
  and and_8 (and_8_out, and_1_out, decoder_1_out6);
  and and_9 (and_9_out, and_1_out, decoder_1_out7);
  D_Flip_Flop d_ff_1 (.clk(and_5_out), .D(in_1[0]), .Q(d_ff_1_q));  // open: Qn, preset, en, reset
  and and_10 (and_10_out, CS, RD, OE);
  D_Flip_Flop d_ff_2 (.clk(and_2_out), .D(in_1[0]), .Q(d_ff_2_q));  // open: Qn, preset, en, reset
  and and_11 (and_11_out, decoder_1_out0, d_ff_2_q);
  D_Flip_Flop d_ff_3 (.clk(and_3_out), .D(in_1[0]), .Q(d_ff_3_q));  // open: Qn, preset, en, reset
  and and_12 (and_12_out, decoder_1_out1, d_ff_3_q);
  D_Flip_Flop d_ff_4 (.clk(and_4_out), .D(in_1[0]), .Q(d_ff_4_q));  // open: Qn, preset, en, reset
  and and_13 (and_13_out, decoder_1_out2, d_ff_4_q);
  and and_14 (and_14_out, decoder_1_out3, d_ff_1_q);
  D_Flip_Flop d_ff_5 (.clk(and_6_out), .D(in_1[0]), .Q(d_ff_5_q));  // open: Qn, preset, en, reset
  and and_15 (and_15_out, decoder_1_out4, d_ff_5_q);
  D_Flip_Flop d_ff_6 (.clk(and_7_out), .D(in_1[0]), .Q(d_ff_6_q));  // open: Qn, preset, en, reset
  and and_16 (and_16_out, decoder_1_out5, d_ff_6_q);
  D_Flip_Flop d_ff_7 (.clk(and_8_out), .D(in_1[0]), .Q(d_ff_7_q));  // open: Qn, preset, en, reset
  and and_17 (and_17_out, decoder_1_out6, d_ff_7_q);
  D_Flip_Flop d_ff_8 (.clk(and_9_out), .D(in_1[0]), .Q(d_ff_8_q));  // open: Qn, preset, en, reset
  and and_18 (and_18_out, decoder_1_out7, d_ff_8_q);
  D_Flip_Flop d_ff_9 (.clk(and_2_out), .D(in_1[1]), .Q(d_ff_9_q));  // open: Qn, preset, en, reset
  and and_19 (and_19_out, decoder_1_out0, d_ff_9_q);
  D_Flip_Flop d_ff_10 (.clk(and_3_out), .D(in_1[1]), .Q(d_ff_10_q));  // open: Qn, preset, en, reset
  and and_20 (and_20_out, decoder_1_out1, d_ff_10_q);
  D_Flip_Flop d_ff_11 (.clk(and_4_out), .D(in_1[1]), .Q(d_ff_11_q));  // open: Qn, preset, en, reset
  and and_21 (and_21_out, decoder_1_out2, d_ff_11_q);
  D_Flip_Flop d_ff_12 (.clk(and_5_out), .D(in_1[1]), .Q(d_ff_12_q));  // open: Qn, preset, en, reset
  and and_22 (and_22_out, decoder_1_out3, d_ff_12_q);
  D_Flip_Flop d_ff_13 (.clk(and_6_out), .D(in_1[1]), .Q(d_ff_13_q));  // open: Qn, preset, en, reset
  and and_23 (and_23_out, decoder_1_out4, d_ff_13_q);
  D_Flip_Flop d_ff_14 (.clk(and_7_out), .D(in_1[1]), .Q(d_ff_14_q));  // open: Qn, preset, en, reset
  and and_24 (and_24_out, decoder_1_out5, d_ff_14_q);
  D_Flip_Flop d_ff_15 (.clk(and_8_out), .D(in_1[1]), .Q(d_ff_15_q));  // open: Qn, preset, en, reset
  and and_25 (and_25_out, decoder_1_out6, d_ff_15_q);
  D_Flip_Flop d_ff_16 (.clk(and_9_out), .D(in_1[1]), .Q(d_ff_16_q));  // open: Qn, preset, en, reset
  and and_26 (and_26_out, decoder_1_out7, d_ff_16_q);
  D_Flip_Flop d_ff_17 (.clk(and_2_out), .D(in_1[2]), .Q(d_ff_17_q));  // open: Qn, preset, en, reset
  and and_27 (and_27_out, decoder_1_out0, d_ff_17_q);
  D_Flip_Flop d_ff_18 (.clk(and_3_out), .D(in_1[2]), .Q(d_ff_18_q));  // open: Qn, preset, en, reset
  and and_28 (and_28_out, decoder_1_out1, d_ff_18_q);
  D_Flip_Flop d_ff_19 (.clk(and_4_out), .D(in_1[2]), .Q(d_ff_19_q));  // open: Qn, preset, en, reset
  and and_29 (and_29_out, decoder_1_out2, d_ff_19_q);
  D_Flip_Flop d_ff_20 (.clk(and_5_out), .D(in_1[2]), .Q(d_ff_20_q));  // open: Qn, preset, en, reset
  and and_30 (and_30_out, decoder_1_out3, d_ff_20_q);
  D_Flip_Flop d_ff_21 (.clk(and_6_out), .D(in_1[2]), .Q(d_ff_21_q));  // open: Qn, preset, en, reset
  and and_31 (and_31_out, decoder_1_out4, d_ff_21_q);
  D_Flip_Flop d_ff_22 (.clk(and_7_out), .D(in_1[2]), .Q(d_ff_22_q));  // open: Qn, preset, en, reset
  and and_32 (and_32_out, decoder_1_out5, d_ff_22_q);
  D_Flip_Flop d_ff_23 (.clk(and_8_out), .D(in_1[2]), .Q(d_ff_23_q));  // open: Qn, preset, en, reset
  and and_33 (and_33_out, decoder_1_out6, d_ff_23_q);
  D_Flip_Flop d_ff_24 (.clk(and_9_out), .D(in_1[2]), .Q(d_ff_24_q));  // open: Qn, preset, en, reset
  and and_34 (and_34_out, decoder_1_out7, d_ff_24_q);
  D_Flip_Flop d_ff_25 (.clk(and_2_out), .D(in_1[3]), .Q(d_ff_25_q));  // open: Qn, preset, en, reset
  D_Flip_Flop d_ff_26 (.clk(and_3_out), .D(in_1[3]), .Q(d_ff_26_q));  // open: Qn, preset, en, reset
  D_Flip_Flop d_ff_27 (.clk(and_4_out), .D(in_1[3]), .Q(d_ff_27_q));  // open: Qn, preset, en, reset
  D_Flip_Flop d_ff_28 (.clk(and_5_out), .D(in_1[3]), .Q(d_ff_28_q));  // open: Qn, preset, en, reset
  and and_35 (and_35_out, decoder_1_out3, d_ff_28_q);
  D_Flip_Flop d_ff_29 (.clk(and_6_out), .D(in_1[3]), .Q(d_ff_29_q));  // open: Qn, preset, en, reset
  D_Flip_Flop d_ff_30 (.clk(and_7_out), .D(in_1[3]), .Q(d_ff_30_q));  // open: Qn, preset, en, reset
  D_Flip_Flop d_ff_31 (.clk(and_8_out), .D(in_1[3]), .Q(d_ff_31_q));  // open: Qn, preset, en, reset
  D_Flip_Flop d_ff_32 (.clk(and_9_out), .D(in_1[3]), .Q(d_ff_32_q));  // open: Qn, preset, en, reset
  and and_36 (and_36_out, decoder_1_out0, d_ff_25_q);
  and and_37 (and_37_out, decoder_1_out1, d_ff_26_q);
  and and_38 (and_38_out, decoder_1_out2, d_ff_27_q);
  and and_39 (and_39_out, decoder_1_out4, d_ff_29_q);
  and and_40 (and_40_out, decoder_1_out5, d_ff_30_q);
  and and_41 (and_41_out, decoder_1_out6, d_ff_31_q);
  and and_42 (and_42_out, decoder_1_out7, d_ff_32_q);
  or or_1 (or_1_out, and_36_out, and_37_out, and_38_out, and_35_out, and_39_out, and_40_out, and_41_out, and_42_out);
  or or_2 (or_2_out, and_28_out, and_29_out, and_30_out, and_31_out, and_32_out, and_33_out, and_34_out, and_27_out);
  or or_3 (or_3_out, and_19_out, and_20_out, and_21_out, and_22_out, and_23_out, and_24_out, and_25_out, and_26_out);
  or or_4 (or_4_out, and_11_out, and_12_out, and_13_out, and_14_out, and_15_out, and_16_out, and_17_out, and_18_out);
  assign out_6[2] = and_10_out ? or_2_out : 1'bz;  // Controlled_Buffer controlled_buffer_1
  assign out_6[1] = and_10_out ? or_3_out : 1'bz;  // Controlled_Buffer controlled_buffer_2
  assign out_6[0] = and_10_out ? or_4_out : 1'bz;  // Controlled_Buffer controlled_buffer_3
  assign out_6[3] = and_10_out ? or_1_out : 1'bz;  // Controlled_Buffer controlled_buffer_4
endmodule

module _1bit_ADDER (
  input  A,
  input  B,
  input  C,
  output S,
  output c_2
);

  wire and_1_out, and_2_out, xor_1_out;

  and and_1 (and_1_out, B, A);
  xor xor_1 (xor_1_out, A, B);
  xor xor_2 (S, xor_1_out, C);
  and and_2 (and_2_out, xor_1_out, C);
  or or_1 (c_2, and_2_out, and_1_out);
endmodule

module ADD_SUB (
  input  k,
  input  [3:0] A,
  input  [3:0] B,
  output [3:0] result,
  output c
);

  wire n1bit_adder_1_c_2, n1bit_adder_2_c_2, n1bit_adder_3_c_2, xor_1_out, xor_2_out, xor_3_out, xor_4_out;

  xor xor_1 (xor_1_out, k, B[0]);
  xor xor_2 (xor_2_out, k, B[1]);
  xor xor_3 (xor_3_out, k, B[2]);
  xor xor_4 (xor_4_out, k, B[3]);
  _1bit_ADDER u_1bit_adder_1 (.A(A[0]), .B(xor_1_out), .C(k), .S(result[0]), .c_2(n1bit_adder_1_c_2));
  _1bit_ADDER u_1bit_adder_2 (.A(A[1]), .B(xor_2_out), .C(n1bit_adder_1_c_2), .S(result[1]), .c_2(n1bit_adder_2_c_2));
  _1bit_ADDER u_1bit_adder_3 (.A(A[2]), .B(xor_3_out), .C(n1bit_adder_2_c_2), .S(result[2]), .c_2(n1bit_adder_3_c_2));
  _1bit_ADDER u_1bit_adder_4 (.A(A[3]), .B(xor_4_out), .C(n1bit_adder_3_c_2), .S(result[3]), .c_2(c));
endmodule

// COMP
module COMPRATOR (
  input  [3:0] A,
  input  [3:0] B,
  output A_B,
  output A_B_2,
  output A___B
);

  wire and_1_out, and_2_out, and_3_out, and_4_out, and_5_out, and_6_out, and_7_out, and_8_out, and_9_out,
       and_10_out, and_11_out, and_12_out, and_13_out, and_14_out, nor_1_out, nor_2_out, nor_3_out,
       nor_4_out, not_1_out, not_2_out, not_3_out, not_4_out, not_5_out, not_6_out, not_7_out, not_8_out;

  not not_1 (not_1_out, A[0]);
  not not_2 (not_2_out, B[0]);
  not not_3 (not_3_out, A[1]);
  not not_4 (not_4_out, B[1]);
  and and_1 (and_1_out, not_1_out, B[0]);
  and and_2 (and_2_out, A[0], not_2_out);
  and and_3 (and_3_out, not_3_out, B[1]);
  and and_4 (and_4_out, A[1], not_4_out);
  not not_5 (not_5_out, A[2]);
  and and_5 (and_5_out, not_5_out, B[2]);
  and and_6 (and_6_out, A[2], not_6_out);
  not not_6 (not_6_out, B[2]);
  not not_7 (not_7_out, A[3]);
  and and_7 (and_7_out, not_7_out, B[3]);
  and and_8 (and_8_out, A[3], not_8_out);
  not not_8 (not_8_out, B[3]);
  nor nor_1 (nor_1_out, and_1_out, and_2_out);
  nor nor_2 (nor_2_out, and_3_out, and_4_out);
  nor nor_3 (nor_3_out, and_5_out, and_6_out);
  nor nor_4 (nor_4_out, and_7_out, and_8_out);
  and and_9 (and_9_out, nor_1_out, and_3_out);
  and and_10 (and_10_out, nor_1_out, and_4_out);
  and and_11 (and_11_out, nor_1_out, nor_2_out, and_5_out);
  and and_12 (and_12_out, nor_1_out, nor_2_out, and_6_out);
  and and_13 (and_13_out, nor_1_out, nor_2_out, nor_3_out, and_7_out);
  and and_14 (and_14_out, nor_1_out, nor_2_out, nor_4_out, and_8_out);
  and and_15 (A___B, nor_1_out, nor_2_out, nor_3_out, nor_4_out);
  or or_1 (A_B, and_1_out, and_9_out, and_11_out, and_13_out);
  or or_2 (A_B_2, and_2_out, and_12_out, and_10_out, and_14_out);
endmodule

module SHIFT (
  input  [3:0] A,
  input  [1:0] in_2,
  input  clock,
  output [3:0] B
);

  wire button_1_out, multiplexer_1_out, multiplexer_2_out, multiplexer_3_out, multiplexer_4_out;

  Multiplexer #(.select(2)) multiplexer_1 (
    .in0(B[3]), .in1(1'b0), .in2(A[2]), .in3(A[3]), .out(multiplexer_1_out), .sel(in_2));  // open: en
  Multiplexer #(.select(2)) multiplexer_2 (
    .in1(A[3]), .in2(A[1]), .in3(A[2]), .out(multiplexer_2_out), .sel(in_2));  // open: in0, en
  Multiplexer #(.select(2)) multiplexer_3 (
    .in1(A[2]), .in2(A[0]), .in3(A[1]), .out(multiplexer_3_out), .sel(in_2));  // open: in0, en
  Multiplexer #(.select(2)) multiplexer_4 (
    .in1(A[1]), .in2(1'b0), .in3(A[0]), .out(multiplexer_4_out), .sel(in_2));  // open: in0, en
  D_Flip_Flop d_ff_1 (.clk(clock), .D(multiplexer_1_out), .Q(B[3]), .reset(button_1_out));  // open: Qn, preset, en
  D_Flip_Flop d_ff_2 (.clk(clock), .D(multiplexer_2_out), .Q(B[2]), .reset(button_1_out));  // open: Qn, preset, en
  D_Flip_Flop d_ff_3 (.clk(clock), .D(multiplexer_3_out), .Q(B[1]), .reset(button_1_out));  // open: Qn, preset, en
  D_Flip_Flop d_ff_4 (.clk(clock), .D(multiplexer_4_out), .Q(B[0]), .reset(button_1_out));  // open: Qn, preset, en
  Button button_1 (.out(button_1_out));
endmodule

module INC (
  input  [3:0] A,
  output [3:0] out_2
);

  ADD_SUB add_sub_1 (.k(1'b0), .A(A), .B(4'b0001), .result(out_2));  // open: c
endmodule

module DEC (
  input  [3:0] A,
  output [3:0] out_2
);

  ADD_SUB add_sub_1 (.k(1'b1), .A(A), .B(4'b0001), .result(out_2));  // open: c
endmodule

// COMPL
module COMPLEMENT (
  input  [3:0] A,
  output [3:0] B
);

  not not_1 (B[0], A[0]);
  not not_2 (B[1], A[1]);
  not not_3 (B[2], A[2]);
  not not_4 (B[3], A[3]);
endmodule
